# Fritzing sketch Driver Station (saved by Fritzing 0.9.3b)
breadboards: 1

parts:
  Part1 = Arduino Nano (Rev3.0) (ICSP)
  R1 = Slide Potentiometer [maximum_resistance=100kΩ]
  M1 = DC Motor
  S1 = Toggle Switch [package=THT]
  S2 = Toggle Switch [package=THT]
  S3 = Toggle Switch [package=THT]
  S4 = Toggle Switch [package=THT]
  S5 = Toggle Switch [package=THT]
  J1 = Screw terminal - 2 pins [package=THT]
  JP1 = Header 8 [package=1x08_smd_alt]
  JP2 = Header 3 [package=screwterminal-3.5mm-3_lock.007s]
  S6 = Square Pushbutton
  R2 = Resistor [tolerance=±5% resistance=220 package="1206 [SMD]"]
  U1 = CAPSENSE_PAD [package=capsense_pad]
  VCC1 = Battery block 9V

nets:
  N1: Part1.D2, S5.COM
  N2: Part1.D3, S4.COM
  N3: Part1.D4, S3.COM
  N4: Part1.D5, S2.COM
  N5: Part1.D6, S1.COM
  N6: Part1.D7, S6.leg0
  N7: Part1.GND, R1.leg1, S1.L2, S2.L2, JP2.2, VCC1.-
  N8: Part1.5V, R1.leg2, S1.L1, S2.L1, S3.L1, S4.L1, S5.L1, JP2.1, S6.leg1
  N9: Part1.A0, R1.wiper
  N10: M1.pin_1, J1.pin2
  N11: M1.pin_2, J1.pin1
  N12: S3.L2, S4.L2, S5.L2
  N13: JP1.1, JP1.2
  N14: JP1.6, JP1.7, JP1.8
  N15: R2.Pin_0, U1.RECEIVE

notes:
  L289N Motor Drive Dual H-Bridge DC Motor Control Module for Arduino
  ENB
  ENA
  OUT 1
  OUT 2
  IN2
  IN1
  +12v
  GND
  +5v
  470K
