# Fritzing sketch DriverStation (saved by Fritzing 0.9.3b)
breadboards: 1

parts:
  R1 = Slide Potentiometer [maximum_resistance=100kΩ]
  S6 = Square Pushbutton
  U2 = SWITCH-SPST-2 [package=switch-spst-vertical]
  U3 = SWITCH-SPST-2 [package=switch-spst-vertical]
  U4 = SWITCH-SPST-2 [package=switch-spst-vertical]
  U5 = SWITCH-SPST-2 [package=switch-spst-vertical]
  U6 = SWITCH-SPST-2 [package=switch-spst-vertical]
  S7 = Square Pushbutton
  S8 = Square Pushbutton
  S9 = Square Pushbutton
  S11 = Round Pushbutton
  S12 = Round Pushbutton
  S10 = Square Pushbutton
  Part1 = Arduino Leonardo (Rev3b)
  M3 = DC Motor
  J3 = Screw terminal - 2 pins [package=THT]
  JP5 = Header 8 [package=1x08_smd_alt]
  U7 = CAPSENSE_PAD [package=capsense_pad]
  VCC3 = Battery block 9V
  R2 = Resistor [tolerance=±5% resistance=470k package="0402 [SMD]"]
  JP6 = Header 3 [package=molex-1x3_lock]

nets:
  N1: R1.leg1, S6.leg1, U2.P, U3.P, U4.P, U5.P, U6.P, S7.leg1, S8.leg1, S9.leg1, S11.leg1, S12.leg1, S10.leg1, Part1.5V, JP6.1
  N2: R1.wiper, Part1.A0
  N3: R1.leg2, Part1.GND, VCC3.-, JP6.2
  N4: S6.leg0, Part1.D8/A8
  N5: U2.O, Part1.D9_PWM/A9
  N6: U3.O, Part1.D7
  N7: U4.O, Part1.D5_PWM
  N8: U5.O, Part1.D3_PWM/SCL
  N9: U6.O, Part1.D1/TX
  N10: S7.leg0, Part1.D6_PWM/A7
  N11: S8.leg0, Part1.D4/A6
  N12: S9.leg0, Part1.D2/SDA
  N13: S11.leg0, Part1.A4
  N14: S12.leg0, Part1.A5
  N15: S10.leg0, Part1.D0/RX
  N16: Part1.D10_PWM/A10, Part1.D11_PWM, JP5.6, JP5.7, JP5.8
  N17: Part1.D12/A11, R2.Pin_1
  N18: Part1.D13_PWM, U7.RECEIVE, R2.Pin_0
  N19: M3.pin_1, M3.pin_2, J3.pin1, J3.pin2
  N20: JP5.1, JP5.2
  N21: VCC3.+, JP6.3

notes:
  +5v
  GND
  +12v
  IN1
  IN2
  OUT 2
  OUT 1
  ENA
  ENB
  L289N Motor Drive Dual H-Bridge DC Motor Control Module for Arduino
  470K
