# Fritzing sketch Lidar-RingLight-Controller (saved by Fritzing 0.9.3b)

parts:
  Teensy_3_2 = Teensy 3.0
  Part1 = Adafruit VL53L0X Time of Flight Distance Sensor [part_number="Adafruit #3317"]
  Part2 = Adafruit VL53L0X Time of Flight Distance Sensor [part_number="Adafruit #3317"]
  Part3 = Adafruit VL53L0X Time of Flight Distance Sensor [part_number="Adafruit #3317"]
  Part4 = 24 NeoPixel Ring [part_number=1586]
  Part5 = LIDAR-Lite
  Part6 = DC-DC Power Module (5v)

nets:
  N1: Teensy_3_2.D7, Part3.XSHUT
  N2: Teensy_3_2.D8, Part2.XSHUT
  N3: Teensy_3_2.D9, Part1.XSHUT
  N4: Teensy_3_2.D11, Part4.IN
  N5: Teensy_3_2.A4/D18, Part1.SDA, Part2.SDA, Part3.SDA, Part5.SDA
  N6: Teensy_3_2.A5/D19, Part1.SCL, Part2.SCL, Part3.SCL, Part5.MODE, Part5.SCL
  GND: Teensy_3_2.AGND, Part1.GND, Part2.GND, Part3.GND, Part4.GND, Part5.GND, Part6.GND*
  VIN: Part1.VIN, Part2.VIN, Part3.VIN, Part4.VDD, Part5.5V, Part6.Vout

custom parts:
  Adafruit VL53L0X Time of Flight Distance Sensor: The VL53L0X is a Time of Flight distance sensor like no other you've used! The sensor contains a very tiny invisible laser source, and a matching sensor. The VL53L0X can detect the "time of flight", or how long the light has taken to bounce back to the sensor. Since it uses a very narrow light source, it is good for determining distance of only the surface directly in front of it. Unlike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
  24 NeoPixel Ring: 24 ultra bright smart LED NeoPixels are arranged in a circle with 2.6" (66mm) outer diameter. The rings are 'chainable' - connect the output pin of one to the input pin of another. Use only one microcontroller pin to control as many as you can chain together! Each LED is addressable as the driver chip is inside the LED. Each one has ~18mA constant current drive so the color will be very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
  LIDAR-Lite: PulsedLight LIDAR-Lite Sensor
  DC-DC Power Module (5v): DC-DC Power Module based con AMS1117-5.0 Input: DC 6~12V (input power must higher 1V than output power); Output: 5V (+/-0.05V error), 800mA
